// Digital circuit MainProcessor.dig as structural Verilog
module MainProcessor (
  input  [15:0] IN,
  input  clk,
  output [15:0] OUT
);

  wire ALUOp, ALUsrc, button_1_out, clk_t, DataSRC, dipswitch_1_out, nclk, OUTen, PCsrc, WriteData, writePTR;
  wire [2:0] OPcode;
  wire [12:0] rom_1_d;
  wire [15:0] addsub_1_p4, bitextender_1_p2, multiplexer_1_out, multiplexer_3_out, multiplexer_4_out, PC_q,
       PCAdder_s, PTR_q, ramdualport_1_d;

  Multiplexer #(.Bits(16)) multiplexer_1 (
    .sel(PCsrc), .in_0(PCAdder_s), .in_1(bitextender_1_p2), .out(multiplexer_1_out));
  Register #(.Bits(16), .isProgramCounter("true")) PC (.D(multiplexer_1_out), .C(clk_t), .en(1'b1), .Q(PC_q));
  Add #(.Bits(16)) PCAdder (.a(PC_q), .b(16'h1), .c_i(1'b0), .s(PCAdder_s));  // open: c_o
  ROM #(.AddrBits(16), .Bits(16)) rom_1 (.A(PC_q), .sel(1'b1), .D({OPcode, rom_1_d}));
  Button button_1 (.out(button_1_out));
  Multiplexer multiplexer_2 (.sel(dipswitch_1_out), .in_0(button_1_out), .in_1(clk), .out(clk_t));
  not not_1 (nclk, clk_t);
  DipSwitch #(.dipDefault("true")) dipswitch_1 (.out(dipswitch_1_out));
  Register #(.Bits(16)) PTR (.D(addsub_1_p4), .C(clk_t), .en(writePTR), .Q(PTR_q));
  // bitExtender bitextender_1: pin names not known; wires that end beside it: rom_1_d, bitextender_1_p2
  Multiplexer #(.Bits(16)) multiplexer_3 (.sel(ALUsrc), .in_0(PTR_q), .in_1(ramdualport_1_d), .out(multiplexer_3_out));
  // addsub addsub_1: pin names not known; wires that end beside it: multiplexer_3_out, bitextender_1_p2, ALUOp, addsub_1_p4
  // ControlLogic controllogic_1: pin names not known; wires that end beside it: OPcode, PCsrc, DataSRC, OUTen, writePTR, WriteData, ALUsrc, ALUOp
  Multiplexer #(.Bits(16)) multiplexer_4 (.sel(DataSRC), .in_0(addsub_1_p4), .in_1(IN), .out(multiplexer_4_out));
  RAMDualPort #(.AddrBits(16), .Bits(16)) ramdualport_1 (
    .A(PTR_q), .Din(multiplexer_4_out), .str(WriteData), .C(clk_t), .ld(1'b1), .D(ramdualport_1_d));
  Register #(.Bits(16)) OUTreg (.D(ramdualport_1_d), .C(clk_t), .en(OUTen), .Q(OUT));

  // Other names for the same wires on the sheet: sys_clk = clk

  // Notes on the sheet:
  //   FetchStage
  //   contents of rom_1 (hex, n*v repeats v):
  //   32*1,219*0,1
  //   DecodeStage
  //   ExecuteStage
  //   MemoryStage
endmodule
